// Logisim project PIC8.circ as structural Verilog: 3 circuits, main circuit main
module main (
);

  wire CLK, not_1_out, regbank_1_write_ram, RST;
  wire [7:0] multiplexer_1_out, regbank_1_endereco_ram, regbank_1_input_ram;

  regBank regbank_1 (
    .clock(CLK), .reset(RST), .output_ram(multiplexer_1_out), .write_ram(regbank_1_write_ram),
    .input_ram(regbank_1_input_ram), .endereco_ram(regbank_1_endereco_ram));  // open: data_in, write_data, endereco_in, endereco_out, data_out
  Multiplexer #(.width(8), .enable("false")) multiplexer_1 (
    .in1(regbank_1_input_ram), .out(multiplexer_1_out), .sel(regbank_1_write_ram));  // open: in0
  RAM ram_1 (
    .addr(regbank_1_endereco_ram), .we(regbank_1_write_ram), .oe(not_1_out), .clk(CLK),
    .data(multiplexer_1_out));
  not not_1 (not_1_out, regbank_1_write_ram);
endmodule

module reg8bits (
  input  [7:0] data_in,
  input  enable,
  input  clock,
  input  reset,
  output [7:0] data_out
);

  wire and_1_out, and_2_out, and_3_out, and_4_out, and_5_out, and_6_out, and_7_out, and_8_out;

  and and_1 (and_1_out, enable, clock);
  and and_2 (and_2_out, enable, clock);
  and and_3 (and_3_out, enable, clock);
  and and_4 (and_4_out, enable, clock);
  and and_5 (and_5_out, enable, clock);
  and and_6 (and_6_out, enable, clock);
  and and_7 (and_7_out, enable, clock);
  and and_8 (and_8_out, enable, clock);
  D_Flip_Flop d_ff_1 (.D(data_in[0]), .clk(and_1_out), .Q(data_out[0]), .reset(reset));  // open: Qn, preset
  D_Flip_Flop d_ff_2 (.D(data_in[1]), .clk(and_2_out), .Q(data_out[1]), .reset(reset));  // open: Qn, preset
  D_Flip_Flop d_ff_3 (.D(data_in[2]), .clk(and_3_out), .Q(data_out[2]), .reset(reset));  // open: Qn, preset
  D_Flip_Flop d_ff_4 (.D(data_in[3]), .clk(and_4_out), .Q(data_out[3]), .reset(reset));  // open: Qn, preset
  D_Flip_Flop d_ff_5 (.D(data_in[4]), .clk(and_5_out), .Q(data_out[4]), .reset(reset));  // open: Qn, preset
  D_Flip_Flop d_ff_6 (.D(data_in[5]), .clk(and_6_out), .Q(data_out[5]), .reset(reset));  // open: Qn, preset
  D_Flip_Flop d_ff_7 (.D(data_in[6]), .clk(and_7_out), .Q(data_out[6]), .reset(reset));  // open: Qn, preset
  D_Flip_Flop d_ff_8 (.D(data_in[7]), .clk(and_8_out), .Q(data_out[7]), .reset(reset));  // open: Qn, preset

  // Other names for the same wires on the sheet: CLK = clock; D0 = data_in[0]; D1 = data_in[1]; D2 = data_in[2];
  //   D3 = data_in[3]; D4 = data_in[4]; D5 = data_in[5]; D6 = data_in[6]; D7 = data_in[7]; ENB = enable; RST = reset
endmodule

module regBank (
  input  [7:0] data_in,
  input  write_data,
  input  [5:0] endereco_in,
  input  [5:0] endereco_out,
  input  clock,
  input  reset,
  input  [7:0] output_ram,
  output [7:0] data_out,
  output write_ram,
  output [7:0] input_ram,
  output [7:0] endereco_ram
);

  wire demultiplexer_1_out0, demultiplexer_1_out1, fsr, portA, portB, s1, s2, s3, s4, s5, s6, s7, s8, s9,
       s10, s11, s12, s13, s14, s15, s16, status, trisA, trisB, work;
  wire [7:0] multiplexer_1_out, multiplexer_2_out, outFsr, outPortA, outPortB, outS1, outS2, outS3, outS4,
       outS5, outS6, outS7, outS8, outS9, outS10, outS11, outS12, outS13, outS14, outS15, outS16, outStatus,
       outTrisA, outTrisB, outWork;

  Demultiplexer #(.enable("false")) demultiplexer_1 (
    .out0(demultiplexer_1_out0), .out1(demultiplexer_1_out1), .in(write_data), .sel(endereco_in[5]));
  Demultiplexer #(.select(5), .enable("false")) demultiplexer_2 (
    .out1(fsr), .out2(trisA), .out3(trisB), .out4(portA), .out5(portB), .out6(s1), .out7(s2), .out8(s3),
    .out9(s4), .out10(s5), .out11(s6), .out12(s7), .out13(s8), .out14(s9), .out15(s10), .out16(s11),
    .out17(s12), .out18(s13), .out19(s14), .out20(s15), .out21(s16), .in(demultiplexer_1_out0),
    .sel(endereco_in[4:0]));  // open: out0, out22, out23, out24, out25, out26, out27, out28, out29, out30, out31
  Demultiplexer #(.select(5), .enable("false")) demultiplexer_3 (
    .out29(status), .out30(write_ram), .out31(work), .in(demultiplexer_1_out1), .sel(endereco_in[4:0]));  // open: out0, out1, out2, out3, out4, out5, out6, out7, out8, out9, out10, out11, out12, out13, out14, out15, out16, out17, out18, out19, out20, out21, out22, out23, out24, out25, out26, out27, out28
  reg8bits u_FSR (.data_in(data_in), .enable(fsr), .clock(clock), .reset(reset), .data_out(endereco_ram));
  reg8bits u_TRISA (.data_in(data_in), .enable(trisA), .clock(clock), .reset(reset), .data_out(outTrisA));
  reg8bits u_TRISB (.data_in(data_in), .enable(trisA), .clock(clock), .reset(reset), .data_out(outTrisB));
  reg8bits u_PORTA (.data_in(data_in), .enable(portA), .clock(clock), .reset(reset), .data_out(outPortA));
  reg8bits u_PORTB (.data_in(data_in), .enable(portB), .clock(clock), .reset(reset), .data_out(outPortB));
  reg8bits u_STATUS (.data_in(data_in), .enable(status), .clock(clock), .reset(reset), .data_out(outStatus));
  reg8bits u_WORK (.data_in(data_in), .enable(work), .clock(clock), .reset(reset), .data_out(outWork));
  reg8bits u_S1 (.data_in(data_in), .enable(s1), .clock(clock), .reset(reset), .data_out(outS1));
  reg8bits u_S2 (.data_in(data_in), .enable(s2), .clock(clock), .reset(reset), .data_out(outS2));
  reg8bits u_S3 (.data_in(data_in), .enable(s3), .clock(clock), .reset(reset), .data_out(outS3));
  reg8bits u_S4 (.data_in(data_in), .enable(s4), .clock(clock), .reset(reset), .data_out(outS4));
  reg8bits u_S5 (.data_in(data_in), .enable(s5), .clock(clock), .reset(reset), .data_out(outS5));
  reg8bits u_S6 (.data_in(data_in), .enable(s6), .clock(clock), .reset(reset), .data_out(outS6));
  reg8bits u_S7 (.data_in(data_in), .enable(s7), .clock(clock), .reset(reset), .data_out(outS7));
  Multiplexer #(.select(5), .width(8), .enable("false")) multiplexer_1 (
    .in0({8{1'b0}}), .in1(outFsr), .in2(outTrisA), .in3(outTrisB), .in4(outPortA), .in5(outPortB),
    .in6(outS1), .in7(outS2), .in8(outS3), .in9(outS4), .in10(outS5), .in11(outS6), .in12(outS7),
    .in13(outS8), .in14(outS9), .in15(outS10), .in16(outS11), .in17(outS12), .in18(outS13), .in19(outS14),
    .in20(outS15), .in21(outS16), .out(multiplexer_1_out), .sel(endereco_out[4:0]));  // open: in22, in23, in24, in25, in26, in27, in28, in29, in30, in31
  Multiplexer #(.select(5), .width(8), .enable("false")) multiplexer_2 (
    .in29(outStatus), .in30(output_ram), .in31(outWork), .out(multiplexer_2_out), .sel(endereco_out[4:0]));  // open: in0, in1, in2, in3, in4, in5, in6, in7, in8, in9, in10, in11, in12, in13, in14, in15, in16, in17, in18, in19, in20, in21, in22, in23, in24, in25, in26, in27, in28
  Multiplexer #(.width(8), .enable("false")) multiplexer_3 (
    .in0(multiplexer_1_out), .in1(multiplexer_2_out), .out(data_out), .sel(endereco_out[5]));
  reg8bits u_S8 (.data_in(data_in), .enable(s8), .clock(clock), .reset(reset), .data_out(outS8));
  reg8bits u_S9 (.data_in(data_in), .enable(s9), .clock(clock), .reset(reset), .data_out(outS9));
  reg8bits u_S10 (.data_in(data_in), .enable(s10), .clock(clock), .reset(reset), .data_out(outS10));
  reg8bits u_S11 (.data_in(data_in), .enable(s11), .clock(clock), .reset(reset), .data_out(outS11));
  reg8bits u_S12 (.data_in(data_in), .enable(s12), .clock(clock), .reset(reset), .data_out(outS12));
  reg8bits u_S13 (.data_in(data_in), .enable(s13), .clock(clock), .reset(reset), .data_out(outS13));
  reg8bits u_S14 (.data_in(data_in), .enable(s14), .clock(clock), .reset(reset), .data_out(outS14));
  reg8bits u_S15 (.data_in(data_in), .enable(s15), .clock(clock), .reset(reset), .data_out(outS15));
  reg8bits u_S16 (.data_in(data_in), .enable(s16), .clock(clock), .reset(reset), .data_out(outS16));

  assign input_ram = data_in;

  // Other names for the same wires on the sheet: clk = clock; dt[7:0] = data_in; indf = write_ram;
  //   outFrs[7:0] = endereco_ram; rst = reset
endmodule
